# Fritzing sketch Servo_poti_ATtiny13 (saved by Fritzing 0.9.3b)
circuit board: 8.46667cm x 5.64444cm
breadboards: 1

parts:
  U1 = POT [package=pot_mammoth]
  J1 = Basic Servo
  U2 = ATTINY13 [package=dip]
  VCC1 = 4 x AAA Battery Mount

nets:
  N1: U1.S, U2.PB2(SCK_ADC1)
  GND: U1.A, J1.gnd, U2.GND, VCC1.-
  VCC: U1.E, J1.vcc, U2.VCC, VCC1.+
  N2: J1.pulse, U2.PB1(MISO)
